// Logisim project 2x4Decoder.circ as structural Verilog: 1 circuit, main circuit main
module main (
  input  A1,
  input  A2,
  output out_3,
  output out_4,
  output out_5,
  output out_6
);

  buf and_1 (out_3, ~A1);  // AND_Gate AND_Gate
  and and_2 (out_4, ~A1, A2);  // AND_Gate
  and and_3 (out_5, A1, ~A2);  // AND_Gate
  and and_4 (out_6, A1, A2);
endmodule
