// Logisim project 3x8 Decoder v1.circ as structural Verilog: 1 circuit, main circuit main
module main (
  input  A1,
  input  A2,
  input  A3,
  output O_1,
  output O_1_2,
  output O_2,
  output O_3,
  output O_4,
  output _0_5,
  output O_6,
  output O_7
);

  and and_1 (O_1, ~A1, ~A2);  // AND_Gate
  and and_2 (O_1_2, ~A1, ~A2, A3);  // AND_Gate
  and and_3 (O_2, ~A1, A2, A3);  // AND_Gate
  and and_4 (O_3, A1, A2, A3);
  and and_5 (O_4, A1, A2, A3);
  and and_6 (_0_5, A1, A2, A3);
  and and_7 (O_6, A1, A2, A3);
  and and_8 (O_7, A1, A2, A3);
endmodule
