// Logisim project 3x8 Decoder v2.circ as structural Verilog: 1 circuit, main circuit main
module main (
  input  A1,
  input  A2,
  input  A3,
  output o0,
  output o1,
  output o2,
  output o3,
  output o4,
  output o5,
  output o6,
  output o7
);

  and and_1 (o0, ~A1, ~A2);  // AND_Gate
  and and_2 (o1, A1, ~A2, ~A3);  // AND_Gate
  and and_3 (o2, ~A1, A2, A3);  // AND_Gate
  and and_4 (o3, A1, A2, A3);
  and and_5 (o4, A1, A2, A3);
  and and_6 (o5, A1, A2, A3);
  and and_7 (o6, A1, A2, A3);
  and and_8 (o7, A1, A2, A3);
endmodule
